// Logisim project Morse_code_EC101_DIGICREW.circ as structural Verilog: 2 circuits, main circuit main
module main (
  output [7:0] out_1,
  output Msb,
  output LSB
);

  wire and_1_out, clock_1_out, Morse_code_input_out, q0, q1, q2, q3, q4, q5, Reset_out, shift_register_2_out,
       shift_register_3_out, shift_register_4_out, t0, t1, t2;
  wire [0:0] shift_register_1_out;
  wire [5:0] register_1_q;
  wire [7:0] rom_2_data;
  wire [7:2] rom_1_data;

  Shift_Register #(.length(32)) shift_register_1 (
    .in(shift_register_4_out), .clk(clock_1_out), .out(shift_register_1_out[0]), .clr(Reset_out));  // open: shift, load, d0, q0, d1, q1, d2, q2, d3, q3, d4, q4, d5, q5, d6, q6, d7, q7, d8, q8, d9, q9, d10, q10, d11, q11, d12, q12, d13, q13, d14, q14, d15, q15, d16, q16, d17, q17, d18, q18, d19, q19, d20, q20, d21, q21, d22, q22, d23, q23, d24, q24, d25, q25, d26, q26, d27, q27, d28, q28, d29, q29, d30, q30, d31, q31
  Shift_Register #(.length(32)) shift_register_2 (
    .in(1'b0), .clk(clock_1_out), .out(shift_register_2_out), .clr(Reset_out));  // open: shift, load, d0, q0, d1, q1, d2, q2, d3, q3, d4, q4, d5, q5, d6, q6, d7, q7, d8, q8, d9, q9, d10, q10, d11, q11, d12, q12, d13, q13, d14, q14, d15, q15, d16, q16, d17, q17, d18, q18, d19, q19, d20, q20, d21, q21, d22, q22, d23, q23, d24, q24, d25, q25, d26, q26, d27, q27, d28, q28, d29, q29, d30, q30, d31, q31
  Clock clock_1 (.out(clock_1_out));
  Button Reset (.out(Reset_out));
  Button Morse_code_input (.out(Morse_code_input_out));
  Shift_Register #(.length(32)) shift_register_3 (
    .in(shift_register_2_out), .clk(clock_1_out), .out(shift_register_3_out), .clr(Reset_out));  // open: shift, load, d0, q0, d1, q1, d2, q2, d3, q3, d4, q4, d5, q5, d6, q6, d7, q7, d8, q8, d9, q9, d10, q10, d11, q11, d12, q12, d13, q13, d14, q14, d15, q15, d16, q16, d17, q17, d18, q18, d19, q19, d20, q20, d21, q21, d22, q22, d23, q23, d24, q24, d25, q25, d26, q26, d27, q27, d28, q28, d29, q29, d30, q30, d31, q31
  ROM #(.addrWidth(4)) rom_1 (
    .addr({t2, t1, t0, shift_register_1_out[0]}), .data({rom_1_data, Msb, LSB}));  // open: sel
  ROM rom_2 (.addr({q5, q4, q3, q2, q1, q0, Msb, LSB}), .data(rom_2_data));  // open: sel
  D_Flip_Flop d_ff_1 (.clk(clock_1_out), .D(rom_1_data[2]), .Q(t0), .reset(Reset_out));  // open: Qn, preset, en
  D_Flip_Flop d_ff_2 (.clk(clock_1_out), .D(rom_1_data[3]), .Q(t1), .reset(Reset_out));  // open: Qn, preset, en
  D_Flip_Flop d_ff_3 (.clk(clock_1_out), .D(rom_1_data[4]), .Q(t2), .reset(Reset_out));  // open: Qn, preset, en
  Register #(.width(6)) register_1 (
    .D({q5, q4, q3, q2, q1, q0}), .Q(register_1_q), .clk(and_1_out), .clr(Reset_out));  // open: en
  and and_1 (and_1_out, rom_2_data[0], clock_1_out);
  Shift_Register #(.length(32)) shift_register_4 (
    .in(shift_register_3_out), .clk(clock_1_out), .out(shift_register_4_out), .clr(Reset_out));  // open: shift, load, d0, q0, d1, q1, d2, q2, d3, q3, d4, q4, d5, q5, d6, q6, d7, q7, d8, q8, d9, q9, d10, q10, d11, q11, d12, q12, d13, q13, d14, q14, d15, q15, d16, q16, d17, q17, d18, q18, d19, q19, d20, q20, d21, q21, d22, q22, d23, q23, d24, q24, d25, q25, d26, q26, d27, q27, d28, q28, d29, q29, d30, q30, d31, q31
  D_Flip_Flop d_ff_4 (.clk(clock_1_out), .D(rom_2_data[1]), .Q(q0), .reset(Reset_out));  // open: Qn, preset, en
  D_Flip_Flop d_ff_5 (.clk(clock_1_out), .D(rom_2_data[2]), .Q(q1), .reset(Reset_out));  // open: Qn, preset, en
  D_Flip_Flop d_ff_6 (.clk(clock_1_out), .D(rom_2_data[3]), .Q(q2), .reset(Reset_out));  // open: Qn, preset, en
  D_Flip_Flop d_ff_7 (.clk(clock_1_out), .D(rom_2_data[4]), .Q(q3), .reset(Reset_out));  // open: Qn, preset, en
  D_Flip_Flop d_ff_8 (.clk(clock_1_out), .D(rom_2_data[5]), .Q(q4), .reset(Reset_out));  // open: Qn, preset, en
  D_Flip_Flop d_ff_9 (.clk(clock_1_out), .D(rom_2_data[6]), .Q(q5), .reset(Reset_out));  // open: Qn, preset, en
  ROM #(.addrWidth(6)) rom_3 (.addr(register_1_q), .data(out_1));  // open: sel

  // Notes on the sheet:
  //   MORSE_CODE_INPUT
  //   DASH_DOT_GAP_DETECT
  //   contents of rom_1 (hex, n*v repeats v):
  //   0 4 d 8 12 12 14 4 18 18 3 3 14 4
  //   MORSE_CODE_INPUT_Electronics
  //   contents of rom_2 (hex, n*v repeats v):
  //   0 2 1c 0 2 4 6 1 4 8 a 1 6 c e 1 8 10 12 1 a 14 0 1 c 16 0 1 e 18 1a 1 10 0 0 1 12 0 0 1 14 0 0 1 16
  //   0 0 1 18 0 0 1 1a 0 0 1 1c 1e 20 1 1e 22 24 1 20 1e 28 1 22 2a 2c 1 24 2e 30 1 26 32 34 1 28 0 0 1
  //   2a 0 0 1 2c 0 0 1 2e 0 0 1 30 0 0 1 32 0 0 1 34 0 0 1
  //   MORSE_CODE_DECODER
  //   0x45 0x4c 0x45 0x43 0x54 0x52 0x4f 0x4e 0x49 0x43 0x53
  //   Expected_output
  //   contents of rom_3 (hex, n*v repeats v):
  //   0 45 49 41 53 55 52 57 48 56 46 4c 50 4a 54 4e 4d 44 4b 47 4b 42 58 43 59 5a 51
  //   OUTPUT IN ASCII 8 BIT
endmodule

module detector_morse (
  input  CLK,
  input  X,
  output OA_MSB,
  output OB,
  output OC_LSB
);

  wire and_1_out, and_2_out, and_3_out, and_4_out, and_5_out, and_6_out, and_7_out, and_8_out, and_9_out,
       and_10_out, and_11_out, and_12_out, and_13_out, d_ff_1_q, d_ff_1_qn, d_ff_2_q, d_ff_2_qn, d_ff_3_q,
       d_ff_3_qn, not_1_out, OA_out, OB_out, or_1_out, or_2_out, or_3_out, or_4_out;

  not not_1 (not_1_out, X);
  D_Flip_Flop d_ff_1 (.clk(CLK), .D(or_2_out), .Q(d_ff_1_q), .Qn(d_ff_1_qn));  // open: preset, en, reset
  D_Flip_Flop d_ff_2 (.clk(CLK), .D(or_3_out), .Q(d_ff_2_q), .Qn(d_ff_2_qn));  // open: preset, en, reset
  D_Flip_Flop d_ff_3 (.clk(CLK), .D(or_1_out), .Q(d_ff_3_q), .Qn(d_ff_3_qn));  // open: preset, en, reset
  and and_1 (and_1_out, d_ff_2_qn, d_ff_3_q, not_1_out);
  and and_2 (and_2_out, d_ff_2_q, d_ff_3_q, X);
  and and_3 (and_3_out, d_ff_1_qn, d_ff_2_qn, d_ff_3_q);
  and and_4 (and_4_out, d_ff_1_q, d_ff_2_q, d_ff_3_qn, not_1_out);
  and and_5 (and_5_out, d_ff_2_q, d_ff_3_qn);
  and and_6 (and_6_out, d_ff_1_q, d_ff_3_qn);
  and and_7 (and_7_out, not_1_out, d_ff_1_qn, d_ff_2_q);
  and and_8 (and_8_out, d_ff_1_q, d_ff_3_q, X);
  and and_9 (and_9_out, d_ff_1_q, d_ff_2_qn, not_1_out);
  and and_10 (and_10_out, d_ff_1_q, d_ff_3_qn, not_1_out);
  or or_1 (or_1_out, X, and_5_out, and_6_out);
  or or_2 (or_2_out, and_7_out, and_8_out, and_9_out, and_10_out);
  or or_3 (or_3_out, and_1_out, and_2_out, and_3_out, and_4_out);
  and and_11 (and_11_out, d_ff_1_qn, d_ff_2_q, d_ff_3_q, X);
  and and_12 (and_12_out, d_ff_1_q, d_ff_2_q, d_ff_3_qn, not_1_out);
  and and_13 (and_13_out, d_ff_1_qn, d_ff_2_qn, d_ff_3_q, not_1_out);
  D_Flip_Flop d_ff_4 (.clk(CLK), .D(OA_out), .Q(OA_MSB));  // open: Qn, preset, en, reset
  and OA (OA_out, d_ff_1_q, d_ff_2_q, d_ff_3_qn, X);
  or u_OB (OB_out, and_11_out, and_12_out);
  or or_4 (or_4_out, and_12_out, and_13_out);
  D_Flip_Flop d_ff_5 (.clk(CLK), .D(OB_out), .Q(OB));  // open: Qn, preset, en, reset
  D_Flip_Flop d_ff_6 (.clk(CLK), .D(or_4_out), .Q(OC_LSB));  // open: Qn, preset, en, reset
endmodule
